# Fritzing sketch SensorLuz (saved by Fritzing 0.9.3b)
breadboards: 1

parts:
  SparkFun = SparkFun ESP8266 Thing
  Componente2 = Adafruit ADS1115 16Bit I2C ADC [part_number="Adafruit #1085"]
  P1 = S1133 Si Photodiode [package="8mm Ceramic [THT]"]
  U1 = LM 358 Dual Op-Amp [package="SO 08 [SMD]"]
  R2 = Resistor [tolerance=±5% resistance=220 package="2010 [SMD]"]

nets:
  GND: SparkFun.GND, Componente2.GND, U1.connector2
  VCC: SparkFun.VCC, Componente2.VDD, U1.connector7
  N1: SparkFun.GPIO2, Componente2.SDA
  N2: SparkFun.GPIO14, Componente2.SCL
  N3: Componente2.AIN3, R2.Pin_1
  N4: P1.cathode, U1.connector3
  N5: U1.connector1, R2.Pin_0

custom parts:
  Adafruit ADS1115 16Bit I2C ADC: For microcontrollers without an analog-to-digital converter or when you want a higher-precision ADC, the ADS1115 provides 16-bit precision at 860 samples/second over I2C. The chip can be configured as 4 single-ended input channels, or two differential channels. As a nice bonus, it even includes a programmable gain amplifier, up to x16, to help boost up smaller single/differential signals to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
